# Fritzing sketch Bluetooth HC-05 (saved by Fritzing 0.9.3b)
breadboards: 1

parts:
  Part2 = Bluetooth HC-05 Macho
  part = Resistor [tolerance=±5% resistance=2k package=THT]
  part_2 = Resistor [tolerance=±5% resistance=1k package=THT]
  Part3 = Arduino Nano (Rev3.0)

nets:
  N1: Part2.TXD, Part3.D0/RX
  N2: Part2.RXD, part.Pin_0, part_2.Pin_1
  VCC: Part2.VCC, Part3.VIN
  GND: Part2.GND, Part3.GND
  N3: part_2.Pin_0, Part3.D1/TX

// code stored in the sketch: Bluetooth HC-05.ino
// Basic Bluetooth sketch HC-05_02
// Connect the HC-05 module and communicate using the serial monitor
//
// The HC-05 defaults to commincation mode when first powered on.
// The default baud rate for communication mode is 9600
//
 
#include <SoftwareSerial.h>
SoftwareSerial BTserial(2, 3); // RX | TX
// Connect the HC-05 TX to Arduino pin 2 RX. 
// Connect the HC-05 RX to Arduino pin 3 TX through a voltage divider.

// Based on http://www.martyncurrey.com/arduino-with-hc-05-bluetooth-module-in-slave-mode/
 
char c = ' ';
  String s;
 
void setup() 
{
    Serial.begin(9600);
    Serial.println("Arduino is ready");

    pinMode(13, OUTPUT);
 
    // HC-05 default serial speed for commincation mode is 9600
    BTserial.begin(9600);  
}
 
void loop()
{
 
    // Keep reading from HC-05 and send to Arduino Serial Monitor
    if (BTserial.available())
    {  
        c = BTserial.read();
        Serial.write(c);

        if (c == '\r' || c == '\n') {
          s = "";
        }
        else {
          s = s + c;
          Serial.print("#");
          Serial.print(s);
          Serial.println("#");
          if (s == "ON" || s == "on") {
            digitalWrite(13, HIGH);
          }
          else if (s == "OFF" || s == "off") {
            digitalWrite(13, LOW);
          }
        }
    }
 
    // Keep reading from Arduino Serial Monitor and send to HC-05
    if (Serial.available())
    {
        c =  Serial.read();
        BTserial.write(c);
    }
 
}
